// Logisim project LC-3.circ as structural Verilog: 17 circuits, main circuit main
module main (
  input  Reset,
  output out_2,
  output out_3,
  output out_4,
  output out_5,
  output out_6,
  output out_7,
  output out_8,
  output [15:0] out_9,
  output [15:0] out_10,
  output [15:0] out_11,
  output [15:0] out_12,
  output [15:0] out_13,
  output [15:0] out_14,
  output [15:0] out_15,
  output [15:0] out_16,
  output [15:0] out_17,
  output halt,
  output [15:0] out_19,
  output [15:0] out_20,
  output [15:0] out_21,
  output [15:0] out_22
);

  wire decodeir_1_writereg, getcst_1_usecst, JSR, LDI_TSI, memory_exit_1_condition, or16_1_out_2,
       or16_2_out_2, or_1_out, ramctrl_1_memload, ramctrl_1_memstore, regpc_1_jsr;
  wire [2:0] multiplexer_1_out, nzp_1_nzp;
  wire [15:0] alu_1_output, getcst_1_cst, memory_exit_1_memout, OffSet9, RegIN, registres_1_out_sr1,
       registres_1_out_sr2;

  BiClock biclock_1 (.reset(Reset), .signal0(out_2), .signal1(out_3));
  RegPC regpc_1 (
    .H(out_3), .PC(out_9), .Reset(Reset), .IR(out_10), .Jump(out_4), .R(registres_1_out_sr1),
    .TestNZP(out_5), .JSR(regpc_1_jsr));
  // Probe on out_9
  // Probe on out_11
  GetAddr getaddr_1 (
    .PC(out_9), .IR(out_10), .Addr(out_11), .Fetch(out_2), .R(registres_1_out_sr1), .Load(out_6),
    .Store(out_7), .LDI_STI(LDI_TSI), .MemOut(out_13), .Exec(out_3), .PC_Offset9(OffSet9));
  // Probe on out_12
  and and_1 (JSR, regpc_1_jsr, out_3, ~out_2);  // AND_Gate
  LED led_1 (.in(out_6));
  RamCtrl ramctrl_1 (
    .Store(out_7), .Fetch(out_2), .Exec(out_3), .Load(out_6), .MemStore(ramctrl_1_memstore),
    .MemLoad(ramctrl_1_memload), .STI_LDI(LDI_TSI), .Offset9(OffSet9), .Addr(out_11));
  LED led_2 (.in(out_7));
  // Probe on out_13
  RAM #(.addrWidth(16), .dataWidth(16), .bus("separate")) ram_1 (
    .addr(out_11), .din(out_12), .data(out_13), .str(ramctrl_1_memstore), .clk(ramctrl_1_memstore),
    .ld(ramctrl_1_memload));  // open: sel, clr
  Register #(.width(16), .trigger("falling")) RegIR (.D(out_13), .Q(out_10), .clk(out_2));  // open: en, clr
  DecodeIR decodeir_1 (.IR(out_10), .Jump(out_4), .WriteReg(decodeir_1_writereg), .Load(out_6), .Store(out_7));
  // Probe on getcst_1_cst
  GetCst getcst_1 (.IR(out_10), .Cst(getcst_1_cst), .UseCst(getcst_1_usecst));
  // Probe on out_10[15:14]
  and and_2 (out_8, decodeir_1_writereg, out_3);
  or or_1 (or_1_out, JSR, out_8);
  // Probe on multiplexer_1_out
  // Probe on out_10[8:6]
  // Probe on out_10[2:0]
  Multiplexer #(.width(3), .enable("false")) multiplexer_1 (
    .in0(out_10[11:9]), .in1(3'b111), .out(multiplexer_1_out), .sel(JSR));
  // Probe on registres_1_out_sr1
  ALU alu_1 (
    .UseCst(getcst_1_usecst), .e2(out_10[15:14]), .Input1(registres_1_out_sr1), .Input2(registres_1_out_sr2),
    .Cst(getcst_1_cst), .Output(alu_1_output));
  Registres registres_1 (
    .SR1(out_10[8:6]), .IN(RegIN), .SR2(out_10[2:0]), .WriteReg(or_1_out), .DR_SR(multiplexer_1_out),
    .OUT_SR1(registres_1_out_sr1), .OUT_SR2(registres_1_out_sr2), .OUT_SR(out_12), .R0(out_14), .R1(out_15),
    .R2(out_16), .R3(out_17), .R4(out_19), .R5(out_20), .R6(out_21), .R7(out_22));
  // Probe on registres_1_out_sr2
  NZP nzp_1 (.RES(RegIN), .NZP(nzp_1_nzp), .IR(out_10), .TestNZP(out_5), .WriteReg(out_8));
  // Probe on nzp_1_nzp
  Or16 or16_1 (.in_1(out_10), .out_2(or16_1_out_2));
  Or16 or16_2 (.in_1(out_9), .out_2(or16_2_out_2));
  // Probe on out_14
  // Probe on out_15
  // Probe on out_16
  // Probe on out_17
  // Probe on out_19
  // Probe on out_20
  // Probe on out_21
  // Probe on out_22
  and and_3 (halt, ~or16_1_out_2, or16_2_out_2);  // AND_Gate
  // Probe on RegIN
  Multiplexer #(.width(16), .enable("false")) multiplexer_2 (
    .in0(alu_1_output), .in1(memory_exit_1_memout), .out(RegIN), .sel(memory_exit_1_condition));
  Memory_Exit memory_exit_1 (
    .IR(out_10), .PC(out_9), .MemIn(out_13), .MemOut(memory_exit_1_memout), .Exec(out_3), .Load(out_6),
    .Condition(memory_exit_1_condition), .JSR(JSR));

  // Other names for the same wires on the sheet: Addr[15:0] = out_11; Condition = out_5; Exec = out_3; Fetch = out_2;
  //   IR[15:0] = out_10; JumpInstr = out_4; Load = out_6; MemOUT[15:0] = out_13; PC[15:0] = out_9; R0[15:0] = out_14;
  //   R1[15:0] = out_15; R2[15:0] = out_16; R3[15:0] = out_17; R4[15:0] = out_19; R5[15:0] = out_20;
  //   R6[15:0] = out_21; R7[15:0] = out_22; MemIN[15:0] = out_12; SR[15:0] = out_12; Store = out_7; WriteReg = out_8

  // Notes on the sheet:
  //   R
  //   IR
  //   R
  //   IR
  //   RAM
  //   Traces (NE PAS MODIFIER)______________________________________________________________________________________________________
  //   Ecriture si WriteReg (Load || Artih)
  //   Ou si JSR/JSRR
  //   (sauvegarde du PC dans R7)
  //   Si JSR/JSSR SR = 7
  //   GetOp
  //   Arret des traces au 1er NOP
  //   si condition =1
  //   RegIn = MemExit
endmodule

module ALU (
  input  [15:0] Input1,
  input  [15:0] Input2,
  input  [15:0] Cst,
  input  UseCst,
  input  [1:0] e2,
  output [15:0] Output
);

  wire [15:0] adder_1_out, and_1_out, multiplexer_1_out, xor_1_out;

  Multiplexer #(.width(16), .enable("false")) multiplexer_1 (
    .in0(Input2), .in1(Cst), .out(multiplexer_1_out), .sel(UseCst));
  Adder #(.width(16)) adder_1 (.a(multiplexer_1_out), .b(Input1), .out(adder_1_out));  // open: cin, cout
  assign and_1_out = Input1 & multiplexer_1_out;  // AND_Gate and_1, 16 bits wide
  Multiplexer #(.select(2), .width(16), .enable("false")) multiplexer_2 (
    .in0(adder_1_out), .in1(and_1_out), .in2(xor_1_out), .out(Output), .sel(e2));  // open: in3
  assign xor_1_out = Input1 ^ multiplexer_1_out;  // XOR_Gate xor_1, 16 bits wide

  // Notes on the sheet:
  //   ADD
  //   AND
  //   NOT + XOR
endmodule

module BiClock (
  input  reset,
  output signal0,
  output signal1
);

  wire and_1_out, horloge_out, not_1_out, register_1_q;

  Clock horloge (.out(horloge_out));
  not not_1 (not_1_out, register_1_q);
  Register #(.width(1), .trigger("falling")) register_1 (
    .D(not_1_out), .Q(register_1_q), .clk(horloge_out), .clr(reset));  // open: en
  and and_1 (and_1_out, horloge_out, ~reset);  // AND_Gate
  and and_2 (signal0, ~register_1_q, and_1_out);  // AND_Gate
  and and_3 (signal1, register_1_q, and_1_out);

  // Notes on the sheet:
  //   Ce module divise une horloge en deux sous-horloges alternées
  //   Chronogrammes :
  //   horloge: 0101010101 signal0: 0100010001 signal1: 000100010
  //   registre 1-bit
  //   Enable
  //   select : 0 / 1
endmodule

module DecodeIR (
  input  [15:0] IR,
  output Jump,
  output Load,
  output Store,
  output WriteReg
);

  wire and_1_out, and_2_out, and_4_out, not_1_out, not_2_out;

  and and_1 (and_1_out, 1'b1, IR[13]);
  not not_1 (not_1_out, and_1_out);
  xor xor_1 (WriteReg, IR[12], IR[13]);
  and and_2 (and_2_out, IR[12], 1'b1);
  not not_2 (not_2_out, and_2_out);
  and and_3 (Store, and_1_out, and_2_out);
  and and_4 (and_4_out, and_2_out, not_1_out);
  and and_5 (Jump, not_1_out, not_2_out);
  and and_6 (Load, and_1_out, not_2_out);
  // Probe on and_4_out

  // Notes on the sheet:
  //   = 1 si bit 13 à vrai
  //   = 1 si bit 12 à vrai
  //   = 1 si 01 ou 10 (Arith ou Load)
  //   = 1 si 11
  //   = 1 si 01
  //   = 1 si 10
  //   = 1 si 00
  //   Types d'instructions
  //   (toujours arith pour l'instant)
  //   Instruction modifiant les registres
endmodule

module GetAddr (
  input  [15:0] IR,
  input  [15:0] R,
  input  Store,
  input  Load,
  input  [15:0] PC,
  input  Fetch,
  input  [15:0] MemOut,
  input  Exec,
  output LDI_STI,
  output [15:0] PC_Offset9,
  output [15:0] Addr
);

  wire and_1_out, and_3_out, or_1_out, or_2_out;
  wire [15:0] adder_2_out, bit_extender_1_out, bit_extender_2_out, multiplexer_1_out, multiplexer_2_out,
       multiplexer_3_out, register_1_q;

  assign bit_extender_1_out = {{7{IR[8]}}, IR[8:0]};  // Bit_Extender bit_extender_1
  Adder #(.width(16)) adder_1 (.a(PC), .b(bit_extender_1_out), .out(PC_Offset9), .cin(1'b1));  // open: cout
  assign bit_extender_2_out = {{10{IR[5]}}, IR[5:0]};  // Bit_Extender bit_extender_2
  Adder #(.width(16)) adder_2 (.a(bit_extender_2_out), .b(R), .out(adder_2_out));  // open: cin, cout
  Register #(.width(16)) register_1 (.D(MemOut), .Q(register_1_q), .clk(Exec));  // open: en, clr
  Multiplexer #(.select(2), .width(16), .enable("false")) multiplexer_1 (
    .in0(PC_Offset9), .in1(adder_2_out), .in2(PC_Offset9), .in3(PC), .out(multiplexer_1_out), .sel(IR[15:14]));
  or or_1 (or_1_out, Store, Load);
  Multiplexer #(.width(16), .enable("false")) multiplexer_2 (
    .in0(PC), .in1(multiplexer_1_out), .out(multiplexer_2_out), .sel(or_1_out));
  Multiplexer #(.width(16), .enable("false")) multiplexer_3 (
    .in0(multiplexer_2_out), .in1(PC), .out(multiplexer_3_out), .sel(Fetch));
  Multiplexer #(.width(16), .enable("false")) multiplexer_4 (
    .in0(multiplexer_3_out), .in1(register_1_q), .out(Addr), .sel(and_1_out));
  and and_1 (and_1_out, Exec, LDI_STI);
  and and_2 (LDI_STI, or_2_out, and_3_out);
  or or_2 (or_2_out, Store, Load);
  and and_3 (and_3_out, ~IR[14], IR[15]);  // AND_Gate

  // Other names for the same wires on the sheet: _15_14[1:0] = IR[15:14]

  // Notes on the sheet:
  //   BaseR
  //   pc + offset9
  //   envois la valeur sortie en mémoire ssi Exec
  //   BaseR + offSet 6
  //   Addr = PC si
  //   !Load & !Store
  //   si b15/14=00 -> LD/ST
  //   ou = 10 -> STI/LDI
  //   Addr = PC+offset9
  //   si 01 -> STR/LDR
  //   Addr = BaseR + offset6
  //   si 11 -> LEA
  //   Addr = PC
  //   si Fetch = 1
  //   Alors Addr = PC
  //   et si Exec = 1
  //   =MemOut si LDI ou STI
  //   =1 si Load ou Store & b15-14 = 10
  //   Adresse Memoire
endmodule

module GetCst (
  input  [15:0] IR,
  output [15:0] Cst,
  output UseCst
);

  assign Cst = {{11{IR[4]}}, IR[4:0]};  // Bit_Extender bit_extender_1

  assign UseCst = IR[5];
endmodule

module NZP (
  input  [15:0] RES,
  input  WriteReg,
  input  [15:0] IR,
  output [2:0] NZP,
  output TestNZP
);

  wire and_1_out, and_2_out, and_3_out;
  wire [2:0] comparator_1_gt;

  and and_1 (and_1_out, NZP[0], IR[9]);
  and and_2 (and_2_out, NZP[1], IR[10]);
  and and_3 (and_3_out, NZP[2], IR[11]);
  // Probe on IR[11:9]
  Comparator #(.width(16)) comparator_1 (
    .a(RES), .b({16{1'b0}}), .gt(comparator_1_gt[0]), .eq(comparator_1_gt[1]), .lt(comparator_1_gt[2]));
  or or_1 (TestNZP, and_1_out, and_2_out, and_3_out);
  Multiplexer #(.width(3), .enable("false")) multiplexer_1 (
    .in0(NZP), .in1(comparator_1_gt), .out(NZP), .sel(WriteReg));

  // Notes on the sheet:
  //   (Instruction courante)
  //   (Resultat du calcul courant)
  //   Calcule le NZP de RES
  //   = 1 si un des test est vérifié
  //   Si !WriteReg NZP ne change pas
  //   (Instruction mettant à jour NZP)
  //   Test de saut
  //   Valeur actuel du registre d'état NZP
endmodule

// Off6
module Offset6 (
  input  [15:0] IR,
  output [15:0] Off6
);

  assign Off6 = {{10{IR[5]}}, IR[5:0]};  // Bit_Extender bit_extender_1
endmodule

// Off9
module Offset9 (
  input  [15:0] IR,
  output [15:0] Off9
);

  assign Off9 = {{7{IR[8]}}, IR[8:0]};  // Bit_Extender bit_extender_1
endmodule

module Or16 (
  input  [15:0] in_1,
  output out_2
);

  wire [3:0] or_1_out;

  assign or_1_out = in_1[3:0] | in_1[7:4] | in_1[11:8] | in_1[15:12];  // OR_Gate or_1, 4 bits wide
  or or_2 (out_2, or_1_out[0], or_1_out[1], or_1_out[2], or_1_out[3]);
endmodule

module RamCtrl (
  input  STI_LDI,
  input  Exec,
  input  Fetch,
  input  Load,
  input  Store,
  input  [15:0] Addr,
  input  [15:0] Offset9,
  output MemLoad,
  output MemStore
);

  wire and_1_out, and_2_out, and_3_out, and_4_out, comparator_1_eq;

  and and_1 (and_1_out, Exec, Load);
  Comparator #(.width(16)) comparator_1 (.a(Addr), .b(Offset9), .eq(comparator_1_eq));  // open: gt, lt
  and and_2 (and_2_out, ~Exec, STI_LDI);  // AND_Gate
  and and_3 (and_3_out, Exec, ~STI_LDI, Store);  // AND_Gate
  or or_1 (MemLoad, Fetch, and_2_out, and_1_out);
  or or_2 (MemStore, and_3_out, and_4_out);
  and and_4 (and_4_out, Exec, Store, STI_LDI, ~comparator_1_eq);  // AND_Gate

  // Notes on the sheet:
  //   =1 Si Load & Exec
  //   Ou si STI/LDI & !Exec
  //   =1 Si Store & Exec & !(SDI/LDI)
  //   Ou si condition ci-dessous
  //   SI STI/LDI & Store
  //   = 1 ssi Exec = 1 & Addr != PC+Offset9
endmodule

module Registres (
  input  [2:0] SR1,
  input  [15:0] IN,
  input  [2:0] SR2,
  input  WriteReg,
  input  [2:0] DR_SR,
  output [15:0] R0,
  output [15:0] OUT_SR1,
  output [15:0] R1,
  output [15:0] R2,
  output [15:0] R3,
  output [15:0] OUT_SR2,
  output [15:0] R4,
  output [15:0] R5,
  output [15:0] OUT_SR,
  output [15:0] R6,
  output [15:0] R7
);

  wire decoder_1_out0, decoder_1_out1, decoder_1_out2, decoder_1_out3, decoder_1_out4, decoder_1_out5,
       decoder_1_out6, decoder_1_out7;

  Decoder #(.select(3), .disabled(0)) decoder_1 (
    .out0(decoder_1_out0), .out1(decoder_1_out1), .out2(decoder_1_out2), .out3(decoder_1_out3),
    .out4(decoder_1_out4), .out5(decoder_1_out5), .out6(decoder_1_out6), .out7(decoder_1_out7), .sel(DR_SR),
    .en(WriteReg));
  Register #(.width(16), .trigger("falling")) u_R0 (.D(IN), .Q(R0), .clk(decoder_1_out0));  // open: en, clr
  Register #(.width(16), .trigger("falling")) u_R1 (.D(IN), .Q(R1), .clk(decoder_1_out1));  // open: en, clr
  Register #(.width(16), .trigger("falling")) u_R2 (.D(IN), .Q(R2), .clk(decoder_1_out2));  // open: en, clr
  Register #(.width(16), .trigger("falling")) u_R3 (.D(IN), .Q(R3), .clk(decoder_1_out3));  // open: en, clr
  Register #(.width(16), .trigger("falling")) u_R4 (.D(IN), .Q(R4), .clk(decoder_1_out4));  // open: en, clr
  Register #(.width(16), .trigger("falling")) u_R5 (.D(IN), .Q(R5), .clk(decoder_1_out5));  // open: en, clr
  Register #(.width(16), .trigger("falling")) u_R6 (.D(IN), .Q(R6), .clk(decoder_1_out6));  // open: en, clr
  Register #(.width(16), .trigger("falling")) u_R7 (.D(IN), .Q(R7), .clk(decoder_1_out7));  // open: en, clr
  Multiplexer #(.select(3), .width(16), .enable("false")) multiplexer_1 (
    .in0(R0), .in1(R1), .in2(R2), .in3(R3), .in4(R4), .in5(R5), .in6(R6), .in7(R7), .out(OUT_SR1), .sel(SR1));
  Multiplexer #(.select(3), .width(16), .enable("false")) multiplexer_2 (
    .in0(R0), .in1(R1), .in2(R2), .in3(R3), .in4(R4), .in5(R5), .in6(R6), .in7(R7), .out(OUT_SR2), .sel(SR2));
  Multiplexer #(.select(3), .width(16), .enable("false")) multiplexer_3 (
    .in0(R0), .in1(R1), .in2(R2), .in3(R3), .in4(R4), .in5(R5), .in6(R6), .in7(R7), .out(OUT_SR), .sel(DR_SR));
endmodule

module RegPC (
  input  Jump,
  input  [15:0] R,
  input  TestNZP,
  input  H,
  input  Reset,
  input  [15:0] IR,
  output JSR,
  output [15:0] PC
);

  wire and_2_out, and_3_out, or_1_out;
  wire [15:0] adder_1_out, bit_extender_1_out, bit_extender_2_out, multiplexer_1_out, multiplexer_2_out,
       multiplexer_3_out, multiplexer_4_out;

  Multiplexer #(.width(16), .enable("false")) multiplexer_1 (
    .in0({16{1'b0}}), .in1(bit_extender_1_out), .out(multiplexer_1_out), .sel(TestNZP));
  assign bit_extender_1_out = {{7{IR[8]}}, IR[8:0]};  // Bit_Extender bit_extender_1
  // Probe on multiplexer_2_out
  Multiplexer #(.width(16), .enable("false")) multiplexer_2 (
    .in0(multiplexer_1_out), .in1(bit_extender_2_out), .out(multiplexer_2_out), .sel(IR[14]));
  assign bit_extender_2_out = {{5{IR[10]}}, IR[10:0]};  // Bit_Extender bit_extender_2
  and and_1 (JSR, Jump, IR[14], ~IR[15]);  // AND_Gate
  Multiplexer #(.width(16), .enable("false")) multiplexer_3 (
    .in0({16{1'b0}}), .in1(multiplexer_2_out), .out(multiplexer_3_out), .sel(Jump));
  and and_2 (and_2_out, Jump, IR[15]);
  and and_3 (and_3_out, Jump, IR[14], ~IR[15], ~IR[11]);  // AND_Gate
  Adder #(.width(16)) adder_1 (.a(PC), .b(multiplexer_3_out), .out(adder_1_out), .cin(1'b1));  // open: cout
  or or_1 (or_1_out, and_2_out, and_3_out);
  Multiplexer #(.width(16), .enable("false")) multiplexer_4 (
    .in0(adder_1_out), .in1(R), .out(multiplexer_4_out), .sel(or_1_out));
  Register #(.width(16), .trigger("falling")) u_PC (.D(multiplexer_4_out), .Q(PC), .clk(H), .clr(Reset));  // open: en

  // Notes on the sheet:
  //   Offset9 si TestNZP,
  //   0 sinon
  //   Instruction courante
  //   Offset9 si BR,
  //   Offset11 si JSR
  //   si Jump, PC + saut
  //   PC+1 sinon
  //   BaseR
  //   Si JMP & b15=1
  //   alors JMP
  //   Si JMP et
  //   si b15=0,b14=1 
  //   et si b11 = 0, alors JSRR
  //   PC <- PC + 1
  //   Si JMP ou JSRR
  //   PC = BaseR
endmodule

module magic_box (
  input  b0,
  input  b1,
  input  b2,
  output [2:0] s
);

  wire not_1_out, not_2_out;
  wire [1:0] bit_extender_1_out, bit_extender_2_out, bit_extender_3_out;
  wire [2:0] adder_1_out, bit_extender_4_out, bit_extender_5_out, bit_extender_6_out, multiplexer_1_out,
       multiplexer_2_out;

  not not_1 (not_1_out, b1);
  not not_2 (not_2_out, b2);
  assign bit_extender_1_out = {{1{1'b0}}, b0};  // Bit_Extender bit_extender_1
  assign bit_extender_2_out = {{1{1'b1}}, not_1_out};  // Bit_Extender bit_extender_2
  assign bit_extender_3_out = {{1{1'b0}}, not_2_out};  // Bit_Extender bit_extender_3
  assign bit_extender_4_out = {{1{1'b0}}, bit_extender_1_out};  // Bit_Extender bit_extender_4
  assign bit_extender_5_out = {{1{1'b0}}, bit_extender_2_out};  // Bit_Extender bit_extender_5
  assign bit_extender_6_out = {{1{1'b1}}, bit_extender_3_out};  // Bit_Extender bit_extender_6
  // Probe on bit_extender_4_out
  Multiplexer #(.width(3), .enable("false")) multiplexer_1 (
    .in0(3'b000), .in1(bit_extender_6_out), .out(multiplexer_1_out), .sel(b2));
  Multiplexer #(.width(3), .enable("false")) multiplexer_2 (
    .in0(3'b000), .in1(bit_extender_5_out), .out(multiplexer_2_out), .sel(b1));
  // Probe on multiplexer_2_out
  // Probe on multiplexer_1_out
  Adder #(.width(3)) adder_1 (.a(multiplexer_2_out), .b(multiplexer_1_out), .out(adder_1_out));  // open: cin, cout
  Adder #(.width(3)) adder_2 (.a(bit_extender_4_out), .b(adder_1_out), .out(s));  // open: cin, cout
endmodule

// Mem exit
module Memory_Exit (
  input  [15:0] IR,
  input  Exec,
  input  [15:0] PC,
  input  Load,
  input  JSR,
  input  [15:0] MemIn,
  output Condition,
  output [15:0] MemOut
);

  wire and_1_out, not_1_out;
  wire [15:0] adder_1_out, adder_2_out, bit_extender_1_out, multiplexer_2_out;

  and and_1 (and_1_out, Exec, Load);
  or or_1 (Condition, and_1_out, JSR);
  not not_1 (not_1_out, JSR);
  Multiplexer #(.width(16), .enable("false")) multiplexer_1 (
    .in0(adder_1_out), .in1(multiplexer_2_out), .out(MemOut), .sel(not_1_out));
  Adder #(.width(16)) adder_1 (.a(PC), .b({16{1'b0}}), .out(adder_1_out), .cin(1'b1));  // open: cout
  Multiplexer #(.select(2), .width(16), .enable("false")) multiplexer_2 (
    .in0(MemIn), .in1(MemIn), .in2(MemIn), .in3(adder_2_out), .out(multiplexer_2_out), .sel(IR[15:14]));
  assign bit_extender_1_out = {{7{IR[8]}}, IR[8:0]};  // Bit_Extender bit_extender_1
  Adder #(.width(16)) adder_2 (.a(bit_extender_1_out), .b(PC), .out(adder_2_out), .cin(1'b1));  // open: cout

  // Notes on the sheet:
  //   Condition = 1 Si Load & Exec (ecriture du de la valeur dans un registre)
  //   Ou si JSR/JSRR (ecriture de PC dans R7)
  //   SI JSR/JSRR MemOut = PC
  //   PC + OffSet si LEA
  //   MemIn sinon
  //   PC + OffSet9 pour LEA
endmodule

module VerrouSR (
  input  H,
  input  E,
  output S
);

  wire and_1_out, and_2_out, not_1_out, not_2_out, not_3_out, or_1_out;

  not not_1 (not_1_out, E);
  and and_1 (and_1_out, H, not_1_out);
  and and_2 (and_2_out, H, E);
  or or_1 (or_1_out, and_1_out, not_2_out);
  not not_2 (not_2_out, S);
  not not_3 (not_3_out, or_1_out);
  or or_2 (S, not_3_out, and_2_out);
endmodule

module Bascule (
  input  Exec,
  input  E,
  output S
);

  wire not_1_out, verrousr_1_s;

  not not_1 (not_1_out, Exec);
  VerrouSR verrousr_1 (.E(E), .H(Exec), .S(verrousr_1_s));
  VerrouSR verrousr_2 (.E(verrousr_1_s), .H(not_1_out), .S(S));
endmodule
